# Fritzing sketch Circuit (saved by Fritzing 0.9.4)
breadboards: 1

parts:
  U1 = NodeMCU V3.0
  S1 = Round Pushbutton
  J1 = Piezo Speaker
  Part1 = Taiway 100-SP-X-T1 SPDT Miniature Toggle Switch [part_number=100-SP-X-T1-0-0-B1-M1 package=THT]  # not connected
  U2 = LIPO-2000mAh [package=lipo-2000]
  TP1 = TP4056 [chip_label=TP4056 package="DIP (Dual Inline) [THT]"]
  U3 = Mini-360 DC-DC Buck converter [package=THT]

nets:
  N1: U1.GND#6, U1.GND#13, U1.GND#16, U1.GND#33, S1.leg1, J1.pin1, TP1.pin5, U3.IN-, U3.OUT-
  N2: U1.D6, S1.leg0
  N3: U1.D7, J1.pin2
  N4: U1.Vin, U3.OUT+
  N5: U2.-, TP1.pin6
  N6: TP1.pin3, U3.IN+

custom parts:
  NodeMCU V3.0: ESP8266 based NodeMCU
  TP4056: A DIP stand-in part for whatever IC you want. With 6 pins on a 300mil dual inline package (DIP) footprint.
  Mini-360 DC-DC Buck converter: Mini-360 DC-DC Buck converter. Tiny buck step down voltage converter, input voltage 4.75 to 23V output 1 to 17V adjustable. Available from ebay and the like.
